// Logisim project cpu_test.circ as structural Verilog: 1 circuit, main circuit main
module main (
  output [31:0] out_1,
  output [31:0] out_2,
  output out_3,
  output [4:0] out_4,
  output [31:0] out_5,
  output halt,
  output out_7,
  output [31:0] out_8,
  output [31:0] out_9
);

  wire clock_1_out, comparator_1_gt;
  wire [5:0] counter_1_q;

  Clock clock_1 (.out(clock_1_out));
  Counter #(.width(6), .max('h3f), .ongoal("stay")) counter_1 (
    .Q(counter_1_q), .carry(halt), .clk(clock_1_out));  // open: load, D, count, clr
  Comparator #(.width(6), .mode("unsigned")) comparator_1 (
    .a(6'b000100), .b(counter_1_q), .gt(comparator_1_gt));  // open: eq, lt
  // Single_Cycle_CPU_ljr_main main_1: pin names not known; wires that end beside it: comparator_1_gt, out_1, out_2, out_3, out_4, out_5, out_7, out_8, out_9
endmodule
